// Logisim project datapath.circ as structural Verilog: 3 circuits, main circuit Datapath
module Datapath (
  input  RegDst,
  input  Branch,
  input  LeMem,
  input  MemparaReg,
  input  ALUOp1,
  input  ALUOp0,
  input  EscreveMem,
  input  OrigALU,
  input  EscreveReg,
  input  Reset,
  input  Clear,
  input  Clear_2,
  output [3:0] Controle_ALU
);

  wire alu_1_p4, and_1_out, Clock_out, control_1_branch, control_1_escrevemem, control_1_escrevereg,
       control_1_lemem, control_1_memparareg, control_1_origalu, control_1_regdst, instructiondecode_1_p1,
       instructiondecode_1_p3, instructiondecode_1_p7, not_1_out, registerfile_1_p2, wordaddress_1_p2,
       wordaddress_2_p2;
  wire [1:0] control_1_opalu;
  wire [3:0] alucontrol_1_out_3;
  wire [4:0] instructiondecode_1_p4, instructiondecode_1_p5, multiplexer_1_out;
  wire [5:0] instructiondecode_1_p2, instructiondecode_1_p6;
  wire [31:0] adder_1_out, branchaddress_1_p3, mips_ram_2_p4, multiplexer_2_out, multiplexer_3_out,
       register_1_q, registerfile_1_p1, registerfile_1_p3, signextend_1_p6, wordaddress_2_p1;

  Register #(.width(32)) register_1 (
    .D(multiplexer_3_out), .Q(register_1_q), .clk(Clock_out), .clr(Reset));  // open: en
  Clock Clock (.out(Clock_out));
  // WordAddress wordaddress_1: pin names not known; wires that end beside it: register_1_q, wordaddress_1_p2, wordaddress_1_p2, 1'b0, 4'b1111
  // InstructionDecode instructiondecode_1: pin names not known; wires that end beside it: instructiondecode_1_p1, instructiondecode_1_p2, instructiondecode_1_p3, instructiondecode_1_p4, instructiondecode_1_p5, instructiondecode_1_p6, instructiondecode_1_p7, {RegDst, Branch, LeMem, MemparaReg, ALUOp1, ALUOp0, EscreveMem, OrigALU, EscreveReg}
  // MIPS_RAM mips_ram_1: pin names not known; wires that end beside it: 1'b0, 1'b1, Clear, instructiondecode_1_p1
  Control control_1 (
    .op(instructiondecode_1_p2), .RegDst(control_1_regdst), .Branch(control_1_branch),
    .LeMem(control_1_lemem), .MemparaReg(control_1_memparareg), .OpALU(control_1_opalu),
    .EscreveMem(control_1_escrevemem), .OrigALU(control_1_origalu), .EscreveReg(control_1_escrevereg));
  Multiplexer #(.width(5), .enable("false")) multiplexer_1 (
    .in0(instructiondecode_1_p4), .in1(instructiondecode_1_p5), .out(multiplexer_1_out),
    .sel(control_1_regdst));
  Adder #(.width(32)) adder_1 (.a(32'h4), .b(register_1_q), .out(adder_1_out));  // open: cin, cout
  not not_1 (not_1_out, Clock_out);
  // SignExtend signextend_1: pin names not known; wires that end beside it: not_1_out, control_1_escrevereg, multiplexer_1_out, instructiondecode_1_p7, instructiondecode_1_p3, signextend_1_p6, instructiondecode_1_p4
  // RegisterFile registerfile_1: pin names not known; wires that end beside it: registerfile_1_p1, registerfile_1_p2, registerfile_1_p3
  Multiplexer #(.width(32), .enable("false")) multiplexer_2 (
    .in0(registerfile_1_p3), .in1(signextend_1_p6), .out(multiplexer_2_out), .sel(control_1_origalu));
  // WordAddress wordaddress_2: pin names not known; wires that end beside it: wordaddress_2_p1, wordaddress_2_p2, wordaddress_2_p2, registerfile_1_p3, control_1_escrevemem, 4'b1111
  ALUcontrol alucontrol_1 (
    .funct(instructiondecode_1_p6), .OpALU(control_1_opalu), .out_3(alucontrol_1_out_3),
    .Operation(Controle_ALU));
  // BranchAddress branchaddress_1: pin names not known; wires that end beside it: adder_1_out, signextend_1_p6, branchaddress_1_p3
  // ALU alu_1: pin names not known; wires that end beside it: registerfile_1_p2, multiplexer_2_out, alucontrol_1_out_3, alu_1_p4, wordaddress_2_p1
  // MIPS_RAM mips_ram_2: pin names not known; wires that end beside it: not_1_out, control_1_lemem, Clear_2, mips_ram_2_p4
  Multiplexer #(.width(32), .enable("false")) multiplexer_3 (
    .in0(adder_1_out), .in1(branchaddress_1_p3), .out(multiplexer_3_out), .sel(and_1_out));
  and and_1 (and_1_out, control_1_branch, alu_1_p4);
  Multiplexer #(.width(32), .enable("false")) multiplexer_4 (
    .in0(wordaddress_2_p1), .in1(mips_ram_2_p4), .out(registerfile_1_p1), .sel(control_1_memparareg));

  // Notes on the sheet:
  //   PC
  //   Opcode
  //   8c0a0000
  //   8c0b0004
  //   014b4820
  //   ac090008
  //   1000ffff
  //   Memória de Instruções
  //   Instruções
  //   Decodificador
  //   main:  lw $t2, 0($zero) 
  //   lw $t3, 4($zero)
  //   add $t1, $t2, $t3
  //   sw $t1, 8($zero)
  //   exit:  beq $zero, $zero, exit
  //   Controle
  //   Controle
  //   lw    001100011
  //   lw    001100011
  //   R     100010001
  //   sw    X00X00110
  //   beq   X10X01000
  //   Extensão
  //   Registradores
  //   Controle ALU
  //   0010 add
  //   0010 add
  //   0010 add
  //   0010 add
  //   0110 sub
  //   ALU
  //   Memória de Dados
  //   Branch
endmodule

module Control (
  input  [5:0] op,
  output RegDst,
  output Branch,
  output LeMem,
  output MemparaReg,
  output [1:0] OpALU,
  output EscreveMem,
  output OrigALU,
  output EscreveReg
);

  and Formato_R (OpALU[0], ~op[5], ~op[4], ~op[3], ~op[2], ~op[1], ~op[0]);  // AND_Gate
  and LW (LeMem, op[5], ~op[4], ~op[3], ~op[2], op[1], op[0]);  // AND_Gate
  and SW (EscreveMem, op[5], ~op[4], op[3], ~op[2], op[1], op[0]);  // AND_Gate
  and BEQ (Branch, ~op[5], ~op[4], ~op[3], op[2], ~op[1], ~op[0]);  // AND_Gate
  or or_1 (OrigALU, LeMem, EscreveMem);
  or or_2 (EscreveReg, OpALU[0], LeMem);

  assign MemparaReg = LeMem;
  assign OpALU[1] = Branch;
  assign RegDst = OpALU[0];
endmodule

module ALUcontrol (
  input  [1:0] OpALU,
  input  [5:0] funct,
  output [3:0] out_3,
  output [3:0] Operation
);

  wire and_1_out, or_1_out;

  or or_1 (or_1_out, funct[3], funct[0]);
  or or_2 (Operation[2], OpALU[1], and_1_out);
  and and_1 (and_1_out, OpALU[0], funct[1]);
  or or_3 (Operation[1], ~OpALU[0], ~funct[2]);  // OR_Gate
  and and_2 (Operation[0], OpALU[0], or_1_out);

  assign Operation[3] = 1'b0;
  assign out_3 = {1'b0, Operation[2:0]};
endmodule
